// Logisim project demoSCRAM2.circ as structural Verilog: 20 circuits, main circuit SCRAM1
module SCRAM1 (
  input  in_1,
  output [7:0] MBRVal,
  output [3:0] MARVal,
  output [3:0] PCVal,
  output [3:0] DVal,
  output [3:0] CVal
);

  wire clock_1_out, controllogicunit1_1_incpc, controllogicunit1_1_mbrtoir, controllogicunit1_1_mtombr,
       controllogicunit1_1_pctomar, decoder_1_out1, decoder_1_out2, decoder_1_out3, decoder_1_out4,
       decoder_1_out5, decoder_1_out6, decoder_1_out7, decoder_1_out8, decoder_1_out9, decoder_2_out0,
       decoder_2_out1, decoder_2_out2, decoder_2_out3, decoder_2_out4, decoder_2_out5, decoder_2_out6,
       decoder_2_out7, decoder_2_out8, decoder_2_out9, not_1_out;
  wire [3:0] timer_1_timerout;
  wire [7:0] ram_1_dout;

  Clock clock_1 (.out(clock_1_out));
  not not_1 (not_1_out, in_1);
  Timer timer_1 (.Clock(clock_1_out), .Inc(in_1), .Clear(not_1_out), .TimerOut(timer_1_timerout));
  ProgramCounter programcounter_1 (.Inc(controllogicunit1_1_incpc), .AddrOut(PCVal));  // open: AddrIn, W
  IR ir_1 (.DataIn(MBRVal), .W(controllogicunit1_1_mbrtoir), .D(DVal), .C(CVal));
  Decoder #(.select(4)) decoder_1 (
    .out1(decoder_1_out1), .out2(decoder_1_out2), .out3(decoder_1_out3), .out4(decoder_1_out4),
    .out5(decoder_1_out5), .out6(decoder_1_out6), .out7(decoder_1_out7), .out8(decoder_1_out8),
    .out9(decoder_1_out9), .sel(CVal), .en(1'b1));  // open: out0, out10, out11, out12, out13, out14, out15
  Decoder #(.select(4)) decoder_2 (
    .out0(decoder_2_out0), .out1(decoder_2_out1), .out2(decoder_2_out2), .out3(decoder_2_out3),
    .out4(decoder_2_out4), .out5(decoder_2_out5), .out6(decoder_2_out6), .out7(decoder_2_out7),
    .out8(decoder_2_out8), .out9(decoder_2_out9), .sel(timer_1_timerout), .en(1'b1));  // open: out10, out11, out12, out13, out14, out15
  MAR mar_1 (.AddrIn(PCVal), .W(controllogicunit1_1_pctomar), .AddrOut(MARVal));
  RAM #(.addrWidth(4), .trigger("high"), .databus("bibus")) ram_1 (
    .addr(MARVal), .we(1'b0), .oe(1'b1), .dout(ram_1_dout));  // open: din
  ControlLogicUnit1 controllogicunit1_1 (
    .Q1(decoder_1_out1), .Q2(decoder_1_out2), .Q3(decoder_1_out3), .Q4(decoder_1_out4), .Q5(decoder_1_out5),
    .Q6(decoder_1_out6), .Q7(decoder_1_out7), .Q8(decoder_1_out8), .Q9(decoder_1_out9), .T0(decoder_2_out0),
    .T1(decoder_2_out1), .T2(decoder_2_out2), .T3(decoder_2_out3), .T4(decoder_2_out4), .T5(decoder_2_out5),
    .T6(decoder_2_out6), .T7(decoder_2_out7), .T8(decoder_2_out8), .T9(decoder_2_out9),
    .PCtoMAR(controllogicunit1_1_pctomar), .MtoMBR(controllogicunit1_1_mtombr),
    .IncPC(controllogicunit1_1_incpc), .MBRtoIR(controllogicunit1_1_mbrtoir));
  MBR mbr_1 (.DataIn(ram_1_dout), .W(controllogicunit1_1_mtombr), .DataOut(MBRVal));

  // Notes on the sheet:
  //   Only instruction fetch
  //   is implemented
endmodule

module ProgramCounter (
  input  Inc,
  input  [3:0] AddrIn,
  input  W,
  output [3:0] AddrOut
);

  wire and_1_out, and_2_out, and_3_out, and_4_out, and_5_out, and_6_out, and_7_out, and_8_out, d_ff_1_qn,
       d_ff_2_qn, d_ff_3_qn, d_ff_4_qn, not_1_out, not_2_out, not_3_out, not_4_out;

  and and_1 (and_1_out, AddrIn[0], W);
  and and_2 (and_2_out, AddrIn[1], W);
  and and_3 (and_3_out, AddrIn[2], W);
  and and_4 (and_4_out, AddrIn[3], W);
  not not_1 (not_1_out, AddrIn[0]);
  not not_2 (not_2_out, AddrIn[1]);
  not not_3 (not_3_out, AddrIn[2]);
  not not_4 (not_4_out, AddrIn[3]);
  and and_5 (and_5_out, not_1_out, W);
  and and_6 (and_6_out, not_2_out, W);
  and and_7 (and_7_out, not_3_out, W);
  and and_8 (and_8_out, not_4_out, W);
  D_Flip_Flop d_ff_1 (.D(d_ff_1_qn), .clk(Inc), .Q(AddrOut[0]), .Qn(d_ff_1_qn), .preset(and_1_out), .reset(and_5_out));
  D_Flip_Flop d_ff_2 (
    .D(d_ff_2_qn), .clk(d_ff_1_qn), .Q(AddrOut[1]), .Qn(d_ff_2_qn), .preset(and_2_out), .reset(and_6_out));
  D_Flip_Flop d_ff_3 (
    .D(d_ff_3_qn), .clk(d_ff_2_qn), .Q(AddrOut[2]), .Qn(d_ff_3_qn), .preset(and_3_out), .reset(and_7_out));
  D_Flip_Flop d_ff_4 (
    .D(d_ff_4_qn), .clk(d_ff_3_qn), .Q(AddrOut[3]), .Qn(d_ff_4_qn), .preset(and_4_out), .reset(and_8_out));

  // Notes on the sheet:
  //   When W=1, AddrIn is stored in counter
endmodule

module MAR (
  input  [3:0] AddrIn,
  input  W,
  output [3:0] AddrOut
);

  Register #(.width(4), .trigger("high")) register_1 (.D(AddrIn), .en(1'b1), .clk(W), .Q(AddrOut));  // open: clr
endmodule

module MBR (
  input  [7:0] DataIn,
  input  W,
  output [7:0] DataOut
);

  Register #(.trigger("high")) register_1 (.D(DataIn), .en(1'b1), .clk(W), .Q(DataOut));  // open: clr
endmodule

module IR (
  input  [7:0] DataIn,
  input  W,
  output [3:0] D,
  output [3:0] C
);

  Register register_1 (.D(DataIn), .en(1'b1), .clk(W), .Q({C, D}));  // open: clr
endmodule

module Timer (
  input  Clock,
  input  Inc,
  input  Clear,
  output [3:0] TimerOut
);

  wire [3:0] adder_1_out, multiplexer_1_out;

  Register #(.width(4)) register_1 (.D(multiplexer_1_out), .en(1'b1), .clk(Clock), .Q(TimerOut));  // open: clr
  Adder #(.width(4)) adder_1 (.a(TimerOut), .b(4'b0001), .out(adder_1_out), .cin(1'b0));  // open: cout
  Multiplexer #(.width(4), .enable("false")) multiplexer_1 (
    .in0(adder_1_out), .in1(4'b0000), .out(multiplexer_1_out), .sel(Clear));

  // Notes on the sheet:
  //   Note that we don't strictly need both Inc and Clear, since they are inversions of each other
  //   The timer is ONLY updated on a positive clock edge!
endmodule

module ControlLogicUnit1 (
  input  Q1,
  input  Q2,
  input  Q3,
  input  Q4,
  input  Q5,
  input  Q6,
  input  Q7,
  input  Q8,
  input  Q9,
  input  T0,
  input  T1,
  input  T2,
  input  T3,
  input  T4,
  input  T5,
  input  T6,
  input  T7,
  input  T8,
  input  T9,
  output PCtoMAR,
  output MtoMBR,
  output IncPC,
  output MBRtoIR
);


  assign IncPC = T1;
  assign MBRtoIR = T2;
  assign MtoMBR = T1;
  assign PCtoMAR = T0;
endmodule

module SCRAM2 (
  output [7:0] MBRVal,
  output [3:0] MARVal,
  output [3:0] PCVal,
  output [3:0] DVal,
  output [3:0] CVal
);

  wire clock_1_out, controllogicunit2_1_incpc, controllogicunit2_1_inctimer, controllogicunit2_1_irdtomar,
       controllogicunit2_1_mbrtoac, controllogicunit2_1_mbrtoir, controllogicunit2_1_mtombr,
       controllogicunit2_1_pctomar, decoder_1_out1, decoder_1_out2, decoder_1_out3, decoder_1_out4,
       decoder_1_out5, decoder_1_out6, decoder_1_out7, decoder_1_out8, decoder_1_out9, decoder_2_out0,
       decoder_2_out1, decoder_2_out2, decoder_2_out3, decoder_2_out4, decoder_2_out5, decoder_2_out6,
       decoder_2_out7, decoder_2_out8, decoder_2_out9, not_1_out, or_1_out;
  wire [3:0] multiplexer_1_out, timer_1_timerout;
  wire [7:0] ram_1_dout;

  Clock clock_1 (.out(clock_1_out));
  not not_1 (not_1_out, controllogicunit2_1_inctimer);
  ProgramCounter programcounter_1 (.Inc(controllogicunit2_1_incpc), .AddrOut(PCVal));  // open: AddrIn, W
  Timer timer_1 (
    .Clock(clock_1_out), .Inc(controllogicunit2_1_inctimer), .Clear(not_1_out), .TimerOut(timer_1_timerout));
  Multiplexer #(.width(4), .enable("false")) multiplexer_1 (
    .in0(PCVal), .in1(DVal), .out(multiplexer_1_out), .sel(controllogicunit2_1_irdtomar));
  or or_1 (or_1_out, controllogicunit2_1_pctomar, controllogicunit2_1_irdtomar);
  IR ir_1 (.DataIn(MBRVal), .W(controllogicunit2_1_mbrtoir), .D(DVal), .C(CVal));
  Decoder #(.select(4)) decoder_1 (
    .out1(decoder_1_out1), .out2(decoder_1_out2), .out3(decoder_1_out3), .out4(decoder_1_out4),
    .out5(decoder_1_out5), .out6(decoder_1_out6), .out7(decoder_1_out7), .out8(decoder_1_out8),
    .out9(decoder_1_out9), .sel(CVal), .en(1'b1));  // open: out0, out10, out11, out12, out13, out14, out15
  Decoder #(.select(4)) decoder_2 (
    .out0(decoder_2_out0), .out1(decoder_2_out1), .out2(decoder_2_out2), .out3(decoder_2_out3),
    .out4(decoder_2_out4), .out5(decoder_2_out5), .out6(decoder_2_out6), .out7(decoder_2_out7),
    .out8(decoder_2_out8), .out9(decoder_2_out9), .sel(timer_1_timerout), .en(1'b1));  // open: out10, out11, out12, out13, out14, out15
  MAR mar_1 (.AddrIn(multiplexer_1_out), .W(or_1_out), .AddrOut(MARVal));
  RAM #(.addrWidth(4), .trigger("high"), .databus("bibus")) ram_1 (
    .addr(MARVal), .we(1'b0), .oe(1'b1), .dout(ram_1_dout));  // open: din
  ControlLogicUnit2 controllogicunit2_1 (
    .Q1(decoder_1_out1), .Q2(decoder_1_out2), .Q3(decoder_1_out3), .Q4(decoder_1_out4), .Q5(decoder_1_out5),
    .Q6(decoder_1_out6), .Q7(decoder_1_out7), .Q8(decoder_1_out8), .Q9(decoder_1_out9), .T0(decoder_2_out0),
    .T1(decoder_2_out1), .T2(decoder_2_out2), .T3(decoder_2_out3), .T4(decoder_2_out4), .T5(decoder_2_out5),
    .T6(decoder_2_out6), .T7(decoder_2_out7), .T8(decoder_2_out8), .T9(decoder_2_out9),
    .PCtoMAR(controllogicunit2_1_pctomar), .MtoMBR(controllogicunit2_1_mtombr),
    .IncPC(controllogicunit2_1_incpc), .MBRtoIR(controllogicunit2_1_mbrtoir),
    .IRDtoMAR(controllogicunit2_1_irdtomar), .MBRtoAC(controllogicunit2_1_mbrtoac),
    .IncTimer(controllogicunit2_1_inctimer));
  Register AC (.D(MBRVal), .en(1'b1), .clk(controllogicunit2_1_mbrtoac));  // open: Q, clr
  MBR mbr_1 (.DataIn(ram_1_dout), .W(controllogicunit2_1_mtombr), .DataOut(MBRVal));

  // Notes on the sheet:
  //   Instructions supported:
  //   lda (1xh)
endmodule

module ControlLogicUnit2 (
  input  Q1,
  input  Q2,
  input  Q3,
  input  Q4,
  input  Q5,
  input  Q6,
  input  Q7,
  input  Q8,
  input  Q9,
  input  T0,
  input  T1,
  input  T2,
  input  T3,
  input  T4,
  input  T5,
  input  T6,
  input  T7,
  input  T8,
  input  T9,
  output PCtoMAR,
  output MtoMBR,
  output IncPC,
  output MBRtoIR,
  output IRDtoMAR,
  output MBRtoAC,
  output IncTimer
);

  wire and_1_out, and_4_out;

  and and_1 (and_1_out, Q1, T4);
  or or_1 (MtoMBR, T1, and_1_out);
  and and_2 (IRDtoMAR, Q1, T3);
  and and_3 (MBRtoAC, Q1, T5);
  and and_4 (and_4_out, Q1, T5);
  nor nor_1 (IncTimer, and_4_out, 1'b0);

  assign IncPC = T1;
  assign MBRtoIR = T2;
  assign PCtoMAR = T0;
endmodule

module SCRAM3 (
  output [7:0] MBRVal,
  output [3:0] MARVal,
  output [3:0] PCVal,
  output [3:0] DVal,
  output [3:0] CVal,
  output [3:0] TimerVal
);

  wire clock_1_out, controllogicunit3_1_incpc, controllogicunit3_1_inctimer, controllogicunit3_1_irdtomar,
       controllogicunit3_1_mbrtoac, controllogicunit3_1_mbrtoir, controllogicunit3_1_mbrtomar,
       controllogicunit3_1_mtombr, controllogicunit3_1_pctomar, decoder_1_out1, decoder_1_out2,
       decoder_1_out3, decoder_1_out4, decoder_1_out5, decoder_1_out6, decoder_1_out7, decoder_1_out8,
       decoder_1_out9, decoder_2_out0, decoder_2_out1, decoder_2_out2, decoder_2_out3, decoder_2_out4,
       decoder_2_out5, decoder_2_out6, decoder_2_out7, decoder_2_out8, decoder_2_out9, not_1_out, or_1_out;
  wire [1:0] priority_encoder_1_out;
  wire [3:0] multiplexer_1_out;
  wire [7:0] ram_1_dout;

  Clock clock_1 (.out(clock_1_out));
  not not_1 (not_1_out, controllogicunit3_1_inctimer);
  Priority_Encoder #(.select(2)) priority_encoder_1 (
    .in0(controllogicunit3_1_pctomar), .in1(controllogicunit3_1_irdtomar),
    .in2(controllogicunit3_1_mbrtomar), .out(priority_encoder_1_out), .en_in(1'b1));  // open: in3, gs, en_out
  ProgramCounter programcounter_1 (.Inc(controllogicunit3_1_incpc), .AddrOut(PCVal));  // open: AddrIn, W
  Timer timer_1 (.Clock(clock_1_out), .Inc(controllogicunit3_1_inctimer), .Clear(not_1_out), .TimerOut(TimerVal));
  Multiplexer #(.select(2), .width(4), .enable("false")) multiplexer_1 (
    .in0(PCVal), .in1(DVal), .in2(MBRVal[3:0]), .out(multiplexer_1_out), .sel(priority_encoder_1_out));  // open: in3
  or or_1 (or_1_out, controllogicunit3_1_pctomar, controllogicunit3_1_mbrtomar, controllogicunit3_1_irdtomar);
  IR ir_1 (.DataIn(MBRVal), .W(controllogicunit3_1_mbrtoir), .D(DVal), .C(CVal));
  Decoder #(.select(4)) decoder_1 (
    .out1(decoder_1_out1), .out2(decoder_1_out2), .out3(decoder_1_out3), .out4(decoder_1_out4),
    .out5(decoder_1_out5), .out6(decoder_1_out6), .out7(decoder_1_out7), .out8(decoder_1_out8),
    .out9(decoder_1_out9), .sel(CVal), .en(1'b1));  // open: out0, out10, out11, out12, out13, out14, out15
  Decoder #(.select(4)) decoder_2 (
    .out0(decoder_2_out0), .out1(decoder_2_out1), .out2(decoder_2_out2), .out3(decoder_2_out3),
    .out4(decoder_2_out4), .out5(decoder_2_out5), .out6(decoder_2_out6), .out7(decoder_2_out7),
    .out8(decoder_2_out8), .out9(decoder_2_out9), .sel(TimerVal), .en(1'b1));  // open: out10, out11, out12, out13, out14, out15
  MAR mar_1 (.AddrIn(multiplexer_1_out), .W(or_1_out), .AddrOut(MARVal));
  RAM #(.addrWidth(4), .trigger("high"), .databus("bibus")) ram_1 (
    .addr(MARVal), .we(1'b0), .oe(1'b1), .dout(ram_1_dout));  // open: din
  ControlLogicUnit3 controllogicunit3_1 (
    .Q1(decoder_1_out1), .Q2(decoder_1_out2), .Q3(decoder_1_out3), .Q4(decoder_1_out4), .Q5(decoder_1_out5),
    .Q6(decoder_1_out6), .Q7(decoder_1_out7), .Q8(decoder_1_out8), .Q9(decoder_1_out9), .T0(decoder_2_out0),
    .T1(decoder_2_out1), .T2(decoder_2_out2), .T3(decoder_2_out3), .T4(decoder_2_out4), .T5(decoder_2_out5),
    .T6(decoder_2_out6), .T7(decoder_2_out7), .T8(decoder_2_out8), .T9(decoder_2_out9),
    .PCtoMAR(controllogicunit3_1_pctomar), .MtoMBR(controllogicunit3_1_mtombr),
    .IncPC(controllogicunit3_1_incpc), .MBRtoIR(controllogicunit3_1_mbrtoir),
    .IRDtoMAR(controllogicunit3_1_irdtomar), .MBRtoAC(controllogicunit3_1_mbrtoac),
    .MBRtoMAR(controllogicunit3_1_mbrtomar), .IncTimer(controllogicunit3_1_inctimer));
  Register AC (.D(MBRVal), .en(1'b1), .clk(controllogicunit3_1_mbrtoac));  // open: Q, clr
  MBR mbr_1 (.DataIn(ram_1_dout), .W(controllogicunit3_1_mtombr), .DataOut(MBRVal));

  // Notes on the sheet:
  //   Instructions supported:
  //   lda (1xh)
  //   ldi (2xh)
endmodule

module ControlLogicUnit3 (
  input  Q1,
  input  Q2,
  input  Q3,
  input  Q4,
  input  Q5,
  input  Q6,
  input  Q7,
  input  Q8,
  input  Q9,
  input  T0,
  input  T1,
  input  T2,
  input  T3,
  input  T4,
  input  T5,
  input  T6,
  input  T7,
  input  T8,
  input  T9,
  output PCtoMAR,
  output MtoMBR,
  output IncPC,
  output MBRtoIR,
  output IRDtoMAR,
  output MBRtoAC,
  output MBRtoMAR,
  output IncTimer
);

  wire and_1_out, and_2_out, and_3_out, and_4_out, and_5_out, and_6_out, and_7_out, and_9_out, and_10_out;

  and and_1 (and_1_out, Q1, T4);
  and and_2 (and_2_out, Q2, T4);
  and and_3 (and_3_out, Q2, T6);
  and and_4 (and_4_out, Q1, T3);
  and and_5 (and_5_out, Q2, T3);
  and and_6 (and_6_out, Q1, T5);
  and and_7 (and_7_out, Q2, T7);
  and and_8 (MBRtoMAR, Q2, T5);
  and and_9 (and_9_out, Q1, T5);
  and and_10 (and_10_out, Q2, T7);
  or or_1 (MtoMBR, T1, and_1_out, and_2_out, and_3_out);
  or or_2 (IRDtoMAR, and_4_out, and_5_out);
  or or_3 (MBRtoAC, and_6_out, and_7_out);
  nor nor_1 (IncTimer, and_9_out, and_10_out, 1'b0);

  assign IncPC = T1;
  assign MBRtoIR = T2;
  assign PCtoMAR = T0;
endmodule

module SCRAM4 (
  output [7:0] MBRVal,
  output [3:0] MARVal,
  output [3:0] PCVal,
  output [3:0] DVal,
  output [3:0] CVal,
  output [3:0] TimerVal
);

  wire clock_1_out, controllogicunit4_1_actom, controllogicunit4_1_incpc, controllogicunit4_1_inctimer,
       controllogicunit4_1_irdtomar, controllogicunit4_1_mbrtoac, controllogicunit4_1_mbrtoir,
       controllogicunit4_1_mbrtomar, controllogicunit4_1_mtombr, controllogicunit4_1_pctomar, decoder_1_out1,
       decoder_1_out2, decoder_1_out3, decoder_1_out4, decoder_1_out5, decoder_1_out6, decoder_1_out7,
       decoder_1_out8, decoder_1_out9, decoder_2_out0, decoder_2_out1, decoder_2_out2, decoder_2_out3,
       decoder_2_out4, decoder_2_out5, decoder_2_out6, decoder_2_out7, decoder_2_out8, decoder_2_out9,
       not_1_out, or_1_out;
  wire [1:0] priority_encoder_1_out;
  wire [3:0] multiplexer_1_out;
  wire [7:0] AC_q, ram_1_dout;

  Clock clock_1 (.out(clock_1_out));
  not not_1 (not_1_out, controllogicunit4_1_inctimer);
  Priority_Encoder #(.select(2)) priority_encoder_1 (
    .in0(controllogicunit4_1_pctomar), .in1(controllogicunit4_1_irdtomar),
    .in2(controllogicunit4_1_mbrtomar), .out(priority_encoder_1_out), .en_in(1'b1));  // open: in3, gs, en_out
  ProgramCounter programcounter_1 (.Inc(controllogicunit4_1_incpc), .AddrOut(PCVal));  // open: AddrIn, W
  Timer timer_1 (.Clock(clock_1_out), .Inc(controllogicunit4_1_inctimer), .Clear(not_1_out), .TimerOut(TimerVal));
  Multiplexer #(.select(2), .width(4), .enable("false")) multiplexer_1 (
    .in0(PCVal), .in1(DVal), .in2(MBRVal[3:0]), .out(multiplexer_1_out), .sel(priority_encoder_1_out));  // open: in3
  or or_1 (or_1_out, controllogicunit4_1_pctomar, controllogicunit4_1_mbrtomar, controllogicunit4_1_irdtomar);
  IR ir_1 (.DataIn(MBRVal), .W(controllogicunit4_1_mbrtoir), .D(DVal), .C(CVal));
  Decoder #(.select(4)) decoder_1 (
    .out1(decoder_1_out1), .out2(decoder_1_out2), .out3(decoder_1_out3), .out4(decoder_1_out4),
    .out5(decoder_1_out5), .out6(decoder_1_out6), .out7(decoder_1_out7), .out8(decoder_1_out8),
    .out9(decoder_1_out9), .sel(CVal), .en(1'b1));  // open: out0, out10, out11, out12, out13, out14, out15
  Decoder #(.select(4)) decoder_2 (
    .out0(decoder_2_out0), .out1(decoder_2_out1), .out2(decoder_2_out2), .out3(decoder_2_out3),
    .out4(decoder_2_out4), .out5(decoder_2_out5), .out6(decoder_2_out6), .out7(decoder_2_out7),
    .out8(decoder_2_out8), .out9(decoder_2_out9), .sel(TimerVal), .en(1'b1));  // open: out10, out11, out12, out13, out14, out15
  MAR mar_1 (.AddrIn(multiplexer_1_out), .W(or_1_out), .AddrOut(MARVal));
  RAM #(.addrWidth(4), .trigger("high"), .databus("bibus")) ram_1 (
    .addr(MARVal), .we(controllogicunit4_1_actom), .oe(1'b1), .din(AC_q), .dout(ram_1_dout));
  ControlLogicUnit4 controllogicunit4_1 (
    .Q1(decoder_1_out1), .Q2(decoder_1_out2), .Q3(decoder_1_out3), .Q4(decoder_1_out4), .Q5(decoder_1_out5),
    .Q6(decoder_1_out6), .Q7(decoder_1_out7), .Q8(decoder_1_out8), .Q9(decoder_1_out9), .T0(decoder_2_out0),
    .T1(decoder_2_out1), .T2(decoder_2_out2), .T3(decoder_2_out3), .T4(decoder_2_out4), .T5(decoder_2_out5),
    .T6(decoder_2_out6), .T7(decoder_2_out7), .T8(decoder_2_out8), .T9(decoder_2_out9),
    .PCtoMAR(controllogicunit4_1_pctomar), .MtoMBR(controllogicunit4_1_mtombr),
    .IncPC(controllogicunit4_1_incpc), .MBRtoIR(controllogicunit4_1_mbrtoir),
    .IRDtoMAR(controllogicunit4_1_irdtomar), .MBRtoAC(controllogicunit4_1_mbrtoac),
    .MBRtoMAR(controllogicunit4_1_mbrtomar), .IncTimer(controllogicunit4_1_inctimer),
    .ACtoM(controllogicunit4_1_actom));
  Register AC (.D(MBRVal), .en(1'b1), .clk(controllogicunit4_1_mbrtoac), .Q(AC_q));  // open: clr
  MBR mbr_1 (.DataIn(ram_1_dout), .W(controllogicunit4_1_mtombr), .DataOut(MBRVal));

  // Notes on the sheet:
  //   Instructions supported:
  //   lda (1xh)
  //   ldi (2xh)
  //   sta (3xh)
endmodule

module ControlLogicUnit4 (
  input  Q1,
  input  Q2,
  input  Q3,
  input  Q4,
  input  Q5,
  input  Q6,
  input  Q7,
  input  Q8,
  input  Q9,
  input  T0,
  input  T1,
  input  T2,
  input  T3,
  input  T4,
  input  T5,
  input  T6,
  input  T7,
  input  T8,
  input  T9,
  output PCtoMAR,
  output MtoMBR,
  output IncPC,
  output MBRtoIR,
  output IRDtoMAR,
  output MBRtoAC,
  output MBRtoMAR,
  output IncTimer,
  output ACtoM
);

  wire and_1_out, and_2_out, and_3_out, and_4_out, and_5_out, and_6_out, and_7_out, and_8_out, and_10_out,
       and_11_out, and_12_out;

  and and_1 (and_1_out, Q1, T4);
  and and_2 (and_2_out, Q2, T4);
  and and_3 (and_3_out, Q2, T6);
  and and_4 (and_4_out, Q1, T3);
  and and_5 (and_5_out, Q2, T3);
  and and_6 (and_6_out, Q3, T3);
  and and_7 (and_7_out, Q1, T5);
  and and_8 (and_8_out, Q2, T7);
  and and_9 (MBRtoMAR, Q2, T5);
  and and_10 (and_10_out, Q1, T5);
  and and_11 (and_11_out, Q2, T7);
  and and_12 (and_12_out, Q3, T4);
  or or_1 (MtoMBR, T1, and_1_out, and_2_out, and_3_out);
  or or_2 (IRDtoMAR, and_4_out, and_5_out, and_6_out);
  or or_3 (MBRtoAC, and_7_out, and_8_out);
  and and_13 (ACtoM, Q3, T4);
  nor nor_1 (IncTimer, and_10_out, and_11_out, and_12_out);

  assign IncPC = T1;
  assign MBRtoIR = T2;
  assign PCtoMAR = T0;
endmodule

module SCRAM5 (
  output [7:0] MBRVal,
  output [3:0] MARVal,
  output [3:0] PCVal,
  output [3:0] DVal,
  output [3:0] CVal,
  output [3:0] TimerVal
);

  wire clock_1_out, controllogicunit5_1_actom, controllogicunit5_1_incpc, controllogicunit5_1_inctimer,
       controllogicunit5_1_irdtomar, controllogicunit5_1_mbrtoac, controllogicunit5_1_mbrtoir,
       controllogicunit5_1_mbrtomar, controllogicunit5_1_mtombr, controllogicunit5_1_pctomar, decoder_1_out1,
       decoder_1_out2, decoder_1_out3, decoder_1_out4, decoder_1_out5, decoder_1_out6, decoder_1_out7,
       decoder_1_out8, decoder_1_out9, decoder_2_out0, decoder_2_out1, decoder_2_out2, decoder_2_out3,
       decoder_2_out4, decoder_2_out5, decoder_2_out6, decoder_2_out7, decoder_2_out8, decoder_2_out9,
       not_1_out, or_1_out;
  wire [1:0] priority_encoder_1_out;
  wire [3:0] multiplexer_1_out;
  wire [7:0] AC_q, ram_1_dout;

  Clock clock_1 (.out(clock_1_out));
  not not_1 (not_1_out, controllogicunit5_1_inctimer);
  Priority_Encoder #(.select(2)) priority_encoder_1 (
    .in0(controllogicunit5_1_pctomar), .in1(controllogicunit5_1_irdtomar),
    .in2(controllogicunit5_1_mbrtomar), .out(priority_encoder_1_out), .en_in(1'b1));  // open: in3, gs, en_out
  ProgramCounter programcounter_1 (.Inc(controllogicunit5_1_incpc), .AddrOut(PCVal));  // open: AddrIn, W
  Timer timer_1 (.Clock(clock_1_out), .Inc(controllogicunit5_1_inctimer), .Clear(not_1_out), .TimerOut(TimerVal));
  Multiplexer #(.select(2), .width(4), .enable("false")) multiplexer_1 (
    .in0(PCVal), .in1(DVal), .in2(MBRVal[3:0]), .out(multiplexer_1_out), .sel(priority_encoder_1_out));  // open: in3
  or or_1 (or_1_out, controllogicunit5_1_pctomar, controllogicunit5_1_mbrtomar, controllogicunit5_1_irdtomar);
  IR ir_1 (.DataIn(MBRVal), .W(controllogicunit5_1_mbrtoir), .D(DVal), .C(CVal));
  Decoder #(.select(4)) decoder_1 (
    .out1(decoder_1_out1), .out2(decoder_1_out2), .out3(decoder_1_out3), .out4(decoder_1_out4),
    .out5(decoder_1_out5), .out6(decoder_1_out6), .out7(decoder_1_out7), .out8(decoder_1_out8),
    .out9(decoder_1_out9), .sel(CVal), .en(1'b1));  // open: out0, out10, out11, out12, out13, out14, out15
  Decoder #(.select(4)) decoder_2 (
    .out0(decoder_2_out0), .out1(decoder_2_out1), .out2(decoder_2_out2), .out3(decoder_2_out3),
    .out4(decoder_2_out4), .out5(decoder_2_out5), .out6(decoder_2_out6), .out7(decoder_2_out7),
    .out8(decoder_2_out8), .out9(decoder_2_out9), .sel(TimerVal), .en(1'b1));  // open: out10, out11, out12, out13, out14, out15
  MAR mar_1 (.AddrIn(multiplexer_1_out), .W(or_1_out), .AddrOut(MARVal));
  RAM #(.addrWidth(4), .trigger("high"), .databus("bibus")) ram_1 (
    .addr(MARVal), .we(controllogicunit5_1_actom), .oe(1'b1), .din(AC_q), .dout(ram_1_dout));
  ControlLogicUnit5 controllogicunit5_1 (
    .Q1(decoder_1_out1), .Q2(decoder_1_out2), .Q3(decoder_1_out3), .Q4(decoder_1_out4), .Q5(decoder_1_out5),
    .Q6(decoder_1_out6), .Q7(decoder_1_out7), .Q8(decoder_1_out8), .Q9(decoder_1_out9), .T0(decoder_2_out0),
    .T1(decoder_2_out1), .T2(decoder_2_out2), .T3(decoder_2_out3), .T4(decoder_2_out4), .T5(decoder_2_out5),
    .T6(decoder_2_out6), .T7(decoder_2_out7), .T8(decoder_2_out8), .T9(decoder_2_out9),
    .PCtoMAR(controllogicunit5_1_pctomar), .MtoMBR(controllogicunit5_1_mtombr),
    .IncPC(controllogicunit5_1_incpc), .MBRtoIR(controllogicunit5_1_mbrtoir),
    .IRDtoMAR(controllogicunit5_1_irdtomar), .MBRtoAC(controllogicunit5_1_mbrtoac),
    .MBRtoMAR(controllogicunit5_1_mbrtomar), .IncTimer(controllogicunit5_1_inctimer),
    .ACtoM(controllogicunit5_1_actom));
  Register AC (.D(MBRVal), .en(1'b1), .clk(controllogicunit5_1_mbrtoac), .Q(AC_q));  // open: clr
  MBR mbr_1 (.DataIn(ram_1_dout), .W(controllogicunit5_1_mtombr), .DataOut(MBRVal));

  // Notes on the sheet:
  //   Instructions supported:
  //   lda (1xh)
  //   ldi (2xh)
  //   sta (3xh)
  //   sti (4xh)
endmodule

module ControlLogicUnit5 (
  input  Q1,
  input  Q2,
  input  Q3,
  input  Q4,
  input  Q5,
  input  Q6,
  input  Q7,
  input  Q8,
  input  Q9,
  input  T0,
  input  T1,
  input  T2,
  input  T3,
  input  T4,
  input  T5,
  input  T6,
  input  T7,
  input  T8,
  input  T9,
  output PCtoMAR,
  output MtoMBR,
  output IncPC,
  output MBRtoIR,
  output IRDtoMAR,
  output MBRtoAC,
  output MBRtoMAR,
  output IncTimer,
  output ACtoM
);

  wire and_1_out, and_2_out, and_3_out, and_4_out, and_5_out, and_6_out, and_7_out, and_8_out, and_9_out,
       and_10_out, and_11_out, and_12_out, and_13_out, and_14_out, and_15_out, and_16_out, and_17_out,
       and_18_out;

  and and_1 (and_1_out, Q1, T4);
  and and_2 (and_2_out, Q2, T4);
  and and_3 (and_3_out, Q2, T6);
  and and_4 (and_4_out, Q4, T4);
  and and_5 (and_5_out, Q1, T3);
  and and_6 (and_6_out, Q2, T3);
  and and_7 (and_7_out, Q3, T3);
  and and_8 (and_8_out, Q4, T3);
  and and_9 (and_9_out, Q1, T5);
  and and_10 (and_10_out, Q2, T7);
  and and_11 (and_11_out, Q1, T5);
  and and_12 (and_12_out, Q2, T7);
  and and_13 (and_13_out, Q3, T4);
  and and_14 (and_14_out, Q4, T6);
  or or_1 (MtoMBR, T1, and_1_out, and_2_out, and_3_out, and_4_out);
  or or_2 (MBRtoAC, and_9_out, and_10_out);
  and and_15 (and_15_out, Q2, T5);
  and and_16 (and_16_out, Q4, T5);
  and and_17 (and_17_out, Q3, T4);
  or or_3 (ACtoM, and_17_out, and_18_out);
  and and_18 (and_18_out, Q4, T6);
  or or_4 (IRDtoMAR, and_5_out, and_6_out, and_7_out, and_8_out);
  or or_5 (MBRtoMAR, and_15_out, and_16_out);
  nor nor_1 (IncTimer, and_11_out, and_12_out, and_13_out, and_14_out);

  assign IncPC = T1;
  assign MBRtoIR = T2;
  assign PCtoMAR = T0;
endmodule

module SCRAM6 (
  output [7:0] MBRVal,
  output [3:0] MARVal,
  output [3:0] PCVal,
  output [3:0] DVal,
  output [3:0] CVal,
  output [7:0] SumOut,
  output CO,
  output Z,
  output [3:0] TimerVal
);

  wire clock_1_out, controllogicunit6_1_actom, controllogicunit6_1_alutoac, controllogicunit6_1_incpc,
       controllogicunit6_1_inctimer, controllogicunit6_1_irdtomar, controllogicunit6_1_mbrtoac,
       controllogicunit6_1_mbrtoir, controllogicunit6_1_mbrtomar, controllogicunit6_1_mtombr,
       controllogicunit6_1_pctomar, decoder_1_out1, decoder_1_out2, decoder_1_out3, decoder_1_out4,
       decoder_1_out5, decoder_1_out6, decoder_1_out7, decoder_1_out8, decoder_1_out9, decoder_2_out0,
       decoder_2_out1, decoder_2_out2, decoder_2_out3, decoder_2_out4, decoder_2_out5, decoder_2_out6,
       decoder_2_out7, decoder_2_out8, decoder_2_out9, not_1_out, or_1_out, or_2_out;
  wire [1:0] priority_encoder_1_out;
  wire [3:0] multiplexer_1_out;
  wire [7:0] AC_q, multiplexer_2_out, ram_1_dout;

  Clock clock_1 (.out(clock_1_out));
  not not_1 (not_1_out, controllogicunit6_1_inctimer);
  Priority_Encoder #(.select(2)) priority_encoder_1 (
    .in0(controllogicunit6_1_pctomar), .in1(controllogicunit6_1_irdtomar),
    .in2(controllogicunit6_1_mbrtomar), .out(priority_encoder_1_out), .en_in(1'b1));  // open: in3, gs, en_out
  ProgramCounter programcounter_1 (.Inc(controllogicunit6_1_incpc), .AddrOut(PCVal));  // open: AddrIn, W
  Timer timer_1 (.Clock(clock_1_out), .Inc(controllogicunit6_1_inctimer), .Clear(not_1_out), .TimerOut(TimerVal));
  Multiplexer #(.select(2), .width(4), .enable("false")) multiplexer_1 (
    .in0(PCVal), .in1(DVal), .in2(MBRVal[3:0]), .out(multiplexer_1_out), .sel(priority_encoder_1_out));  // open: in3
  or or_1 (or_1_out, controllogicunit6_1_pctomar, controllogicunit6_1_mbrtomar, controllogicunit6_1_irdtomar);
  IR ir_1 (.DataIn(MBRVal), .W(controllogicunit6_1_mbrtoir), .D(DVal), .C(CVal));
  Decoder #(.select(4)) decoder_1 (
    .out1(decoder_1_out1), .out2(decoder_1_out2), .out3(decoder_1_out3), .out4(decoder_1_out4),
    .out5(decoder_1_out5), .out6(decoder_1_out6), .out7(decoder_1_out7), .out8(decoder_1_out8),
    .out9(decoder_1_out9), .sel(CVal), .en(1'b1));  // open: out0, out10, out11, out12, out13, out14, out15
  Decoder #(.select(4)) decoder_2 (
    .out0(decoder_2_out0), .out1(decoder_2_out1), .out2(decoder_2_out2), .out3(decoder_2_out3),
    .out4(decoder_2_out4), .out5(decoder_2_out5), .out6(decoder_2_out6), .out7(decoder_2_out7),
    .out8(decoder_2_out8), .out9(decoder_2_out9), .sel(TimerVal), .en(1'b1));  // open: out10, out11, out12, out13, out14, out15
  MAR mar_1 (.AddrIn(multiplexer_1_out), .W(or_1_out), .AddrOut(MARVal));
  RAM #(.addrWidth(4), .trigger("high"), .databus("bibus")) ram_1 (
    .addr(MARVal), .we(controllogicunit6_1_actom), .oe(1'b1), .din(AC_q), .dout(ram_1_dout));
  ControlLogicUnit6 controllogicunit6_1 (
    .Q1(decoder_1_out1), .Q2(decoder_1_out2), .Q3(decoder_1_out3), .Q4(decoder_1_out4), .Q5(decoder_1_out5),
    .Q6(decoder_1_out6), .Q7(decoder_1_out7), .Q8(decoder_1_out8), .Q9(decoder_1_out9), .T0(decoder_2_out0),
    .T1(decoder_2_out1), .T2(decoder_2_out2), .T3(decoder_2_out3), .T4(decoder_2_out4), .T5(decoder_2_out5),
    .T6(decoder_2_out6), .T7(decoder_2_out7), .T8(decoder_2_out8), .T9(decoder_2_out9),
    .PCtoMAR(controllogicunit6_1_pctomar), .MtoMBR(controllogicunit6_1_mtombr),
    .IncPC(controllogicunit6_1_incpc), .MBRtoIR(controllogicunit6_1_mbrtoir),
    .IRDtoMAR(controllogicunit6_1_irdtomar), .MBRtoAC(controllogicunit6_1_mbrtoac),
    .MBRtoMAR(controllogicunit6_1_mbrtomar), .IncTimer(controllogicunit6_1_inctimer),
    .ACtoM(controllogicunit6_1_actom), .ALUtoAC(controllogicunit6_1_alutoac));
  Multiplexer #(.width(8), .enable("false")) multiplexer_2 (
    .in0(SumOut), .in1(MBRVal), .out(multiplexer_2_out), .sel(controllogicunit6_1_mbrtoac));
  or or_2 (or_2_out, controllogicunit6_1_mbrtoac, controllogicunit6_1_alutoac);
  MBR mbr_1 (.DataIn(ram_1_dout), .W(controllogicunit6_1_mtombr), .DataOut(MBRVal));
  Register AC (.D(multiplexer_2_out), .en(1'b1), .clk(or_2_out), .Q(AC_q));  // open: clr
  ALU alu_1 (.CI(1'b0), .A(AC_q), .B(MBRVal), .Sum(SumOut), .CO(CO), .Z(Z));

  // Notes on the sheet:
  //   Instructions supported:
  //   lda (1xh)
  //   ldi (2xh)
  //   sta (3xh)
  //   sti (4xh)
  //   add (5x)
endmodule

module ControlLogicUnit6 (
  input  Q1,
  input  Q2,
  input  Q3,
  input  Q4,
  input  Q5,
  input  Q6,
  input  Q7,
  input  Q8,
  input  Q9,
  input  T0,
  input  T1,
  input  T2,
  input  T3,
  input  T4,
  input  T5,
  input  T6,
  input  T7,
  input  T8,
  input  T9,
  output PCtoMAR,
  output MtoMBR,
  output IncPC,
  output MBRtoIR,
  output IRDtoMAR,
  output MBRtoAC,
  output MBRtoMAR,
  output IncTimer,
  output ACtoM,
  output ALUtoAC
);

  wire and_1_out, and_2_out, and_3_out, and_4_out, and_5_out, and_6_out, and_7_out, and_8_out, and_9_out,
       and_10_out, and_11_out, and_12_out, and_13_out, and_14_out, and_15_out, and_16_out, and_17_out,
       and_18_out, and_19_out, and_20_out, and_21_out;

  and and_1 (and_1_out, Q1, T4);
  and and_2 (and_2_out, Q2, T4);
  and and_3 (and_3_out, Q2, T6);
  and and_4 (and_4_out, Q4, T4);
  and and_5 (and_5_out, Q5, T4);
  and and_6 (and_6_out, Q1, T3);
  and and_7 (and_7_out, Q2, T3);
  and and_8 (and_8_out, Q3, T3);
  and and_9 (and_9_out, Q4, T3);
  and and_10 (and_10_out, Q5, T3);
  and and_11 (and_11_out, Q1, T5);
  and and_12 (and_12_out, Q2, T7);
  and and_13 (and_13_out, Q1, T5);
  and and_14 (and_14_out, Q2, T7);
  and and_15 (and_15_out, Q3, T4);
  and and_16 (and_16_out, Q4, T6);
  and and_17 (and_17_out, Q5, T5);
  or or_1 (MBRtoAC, and_11_out, and_12_out);
  and and_18 (and_18_out, Q2, T5);
  and and_19 (and_19_out, Q4, T5);
  and and_20 (and_20_out, Q3, T4);
  or or_2 (ACtoM, and_20_out, and_21_out);
  and and_21 (and_21_out, Q4, T6);
  and and_22 (ALUtoAC, Q5, T5);
  or or_3 (MtoMBR, T1, and_1_out, and_2_out, and_3_out, and_4_out, and_5_out);
  or or_4 (IRDtoMAR, and_6_out, and_7_out, and_8_out, and_9_out, and_10_out);
  or or_5 (MBRtoMAR, and_18_out, and_19_out);
  nor nor_1 (IncTimer, and_13_out, and_14_out, and_15_out, and_16_out, and_17_out);

  assign IncPC = T1;
  assign MBRtoIR = T2;
  assign PCtoMAR = T0;
endmodule

module ALU (
  input  CI,
  input  [7:0] A,
  input  [7:0] B,
  output [7:0] Sum,
  output CO,
  output Z
);

  Adder adder_1 (.a(A), .b(B), .out(Sum), .cin(CI), .cout(CO));
  nor nor_1 (Z, Sum[0], Sum[1], Sum[2], Sum[3], Sum[4], Sum[5], Sum[6], Sum[7]);
endmodule

module SCRAM7 (
  output [7:0] MBRVal,
  output [3:0] MARVal,
  output [3:0] PCVal,
  output [3:0] DVal,
  output [3:0] CVal,
  output [7:0] SumOut,
  output CO,
  output Z,
  output [3:0] TimerVal
);

  wire clock_1_out, controllogicunit7_1_actom, controllogicunit7_1_alutoac, controllogicunit7_1_incpc,
       controllogicunit7_1_inctimer, controllogicunit7_1_irdtomar, controllogicunit7_1_mbrtoac,
       controllogicunit7_1_mbrtoir, controllogicunit7_1_mbrtomar, controllogicunit7_1_mtombr,
       controllogicunit7_1_pctomar, decoder_1_out1, decoder_1_out2, decoder_1_out3, decoder_1_out4,
       decoder_1_out5, decoder_1_out6, decoder_1_out7, decoder_1_out8, decoder_1_out9, decoder_2_out0,
       decoder_2_out1, decoder_2_out2, decoder_2_out3, decoder_2_out4, decoder_2_out5, decoder_2_out6,
       decoder_2_out7, decoder_2_out8, decoder_2_out9, not_1_out, or_1_out, or_2_out;
  wire [1:0] priority_encoder_1_out;
  wire [3:0] multiplexer_1_out;
  wire [7:0] AC_q, multiplexer_2_out, ram_1_dout;

  Clock clock_1 (.out(clock_1_out));
  not not_1 (not_1_out, controllogicunit7_1_inctimer);
  Priority_Encoder #(.select(2)) priority_encoder_1 (
    .in0(controllogicunit7_1_pctomar), .in1(controllogicunit7_1_irdtomar),
    .in2(controllogicunit7_1_mbrtomar), .out(priority_encoder_1_out), .en_in(1'b1));  // open: in3, gs, en_out
  ProgramCounter programcounter_1 (.Inc(controllogicunit7_1_incpc), .AddrOut(PCVal));  // open: AddrIn, W
  Timer timer_1 (.Clock(clock_1_out), .Inc(controllogicunit7_1_inctimer), .Clear(not_1_out), .TimerOut(TimerVal));
  Multiplexer #(.select(2), .width(4), .enable("false")) multiplexer_1 (
    .in0(PCVal), .in1(DVal), .in2(MBRVal[3:0]), .out(multiplexer_1_out), .sel(priority_encoder_1_out));  // open: in3
  or or_1 (or_1_out, controllogicunit7_1_pctomar, controllogicunit7_1_mbrtomar, controllogicunit7_1_irdtomar);
  IR ir_1 (.DataIn(MBRVal), .W(controllogicunit7_1_mbrtoir), .D(DVal), .C(CVal));
  Decoder #(.select(4)) decoder_1 (
    .out1(decoder_1_out1), .out2(decoder_1_out2), .out3(decoder_1_out3), .out4(decoder_1_out4),
    .out5(decoder_1_out5), .out6(decoder_1_out6), .out7(decoder_1_out7), .out8(decoder_1_out8),
    .out9(decoder_1_out9), .sel(CVal), .en(1'b1));  // open: out0, out10, out11, out12, out13, out14, out15
  Decoder #(.select(4)) decoder_2 (
    .out0(decoder_2_out0), .out1(decoder_2_out1), .out2(decoder_2_out2), .out3(decoder_2_out3),
    .out4(decoder_2_out4), .out5(decoder_2_out5), .out6(decoder_2_out6), .out7(decoder_2_out7),
    .out8(decoder_2_out8), .out9(decoder_2_out9), .sel(TimerVal), .en(1'b1));  // open: out10, out11, out12, out13, out14, out15
  MAR mar_1 (.AddrIn(multiplexer_1_out), .W(or_1_out), .AddrOut(MARVal));
  RAM #(.addrWidth(4), .trigger("high"), .databus("bibus")) ram_1 (
    .addr(MARVal), .we(controllogicunit7_1_actom), .oe(1'b1), .din(AC_q), .dout(ram_1_dout));
  ControlLogicUnit7 controllogicunit7_1 (
    .Q1(decoder_1_out1), .Q2(decoder_1_out2), .Q3(decoder_1_out3), .Q4(decoder_1_out4), .Q5(decoder_1_out5),
    .Q6(decoder_1_out6), .Q7(decoder_1_out7), .Q8(decoder_1_out8), .Q9(decoder_1_out9), .T0(decoder_2_out0),
    .T1(decoder_2_out1), .T2(decoder_2_out2), .T3(decoder_2_out3), .T4(decoder_2_out4), .T5(decoder_2_out5),
    .T6(decoder_2_out6), .T7(decoder_2_out7), .T8(decoder_2_out8), .T9(decoder_2_out9),
    .PCtoMAR(controllogicunit7_1_pctomar), .MtoMBR(controllogicunit7_1_mtombr),
    .IncPC(controllogicunit7_1_incpc), .MBRtoIR(controllogicunit7_1_mbrtoir),
    .IRDtoMAR(controllogicunit7_1_irdtomar), .MBRtoAC(controllogicunit7_1_mbrtoac),
    .MBRtoMAR(controllogicunit7_1_mbrtomar), .IncTimer(controllogicunit7_1_inctimer),
    .ACtoM(controllogicunit7_1_actom), .ALUtoAC(controllogicunit7_1_alutoac));
  Multiplexer #(.width(8), .enable("false")) multiplexer_2 (
    .in0(SumOut), .in1(MBRVal), .out(multiplexer_2_out), .sel(controllogicunit7_1_mbrtoac));
  or or_2 (or_2_out, controllogicunit7_1_mbrtoac, controllogicunit7_1_alutoac);
  MBR mbr_1 (.DataIn(ram_1_dout), .W(controllogicunit7_1_mtombr), .DataOut(MBRVal));
  Register AC (.D(multiplexer_2_out), .en(1'b1), .clk(or_2_out), .Q(AC_q));  // open: clr
  ALU alu_1 (.CI(1'b0), .A(AC_q), .B(MBRVal), .Sum(SumOut), .CO(CO), .Z(Z));

  // Notes on the sheet:
  //   Instructions supported:
  //   lda (1xh)
  //   ldi (2xh)
  //   sta (3xh)
  //   sti (4xh)
  //   add (5x)
endmodule

module ControlLogicUnit7 (
  input  Q1,
  input  Q2,
  input  Q3,
  input  Q4,
  input  Q5,
  input  Q6,
  input  Q7,
  input  Q8,
  input  Q9,
  input  T0,
  input  T1,
  input  T2,
  input  T3,
  input  T4,
  input  T5,
  input  T6,
  input  T7,
  input  T8,
  input  T9,
  output PCtoMAR,
  output MtoMBR,
  output IncPC,
  output MBRtoIR,
  output IRDtoMAR,
  output MBRtoAC,
  output MBRtoMAR,
  output IncTimer,
  output ACtoM,
  output ALUtoAC
);

  wire and_1_out, and_2_out, and_3_out, and_4_out, and_5_out, and_6_out, and_7_out, and_8_out, and_9_out,
       and_10_out, and_11_out, and_12_out, and_13_out, and_14_out, and_15_out, and_16_out, and_17_out,
       and_18_out, and_19_out, and_20_out, and_21_out;

  and and_1 (and_1_out, Q1, T4);
  and and_2 (and_2_out, Q2, T4);
  and and_3 (and_3_out, Q2, T6);
  and and_4 (and_4_out, Q4, T4);
  and and_5 (and_5_out, Q5, T4);
  and and_6 (and_6_out, Q1, T3);
  and and_7 (and_7_out, Q2, T3);
  and and_8 (and_8_out, Q3, T3);
  and and_9 (and_9_out, Q4, T3);
  and and_10 (and_10_out, Q5, T3);
  and and_11 (and_11_out, Q1, T5);
  and and_12 (and_12_out, Q2, T7);
  and and_13 (and_13_out, Q1, T5);
  and and_14 (and_14_out, Q2, T7);
  and and_15 (and_15_out, Q3, T4);
  and and_16 (and_16_out, Q4, T6);
  and and_17 (and_17_out, Q5, T5);
  or or_1 (MBRtoAC, and_11_out, and_12_out);
  and and_18 (and_18_out, Q2, T5);
  and and_19 (and_19_out, Q4, T5);
  and and_20 (and_20_out, Q3, T4);
  or or_2 (ACtoM, and_20_out, and_21_out);
  and and_21 (and_21_out, Q4, T6);
  and and_22 (ALUtoAC, Q5, T5);
  or or_3 (MtoMBR, T1, and_1_out, and_2_out, and_3_out, and_4_out, and_5_out);
  or or_4 (IRDtoMAR, and_6_out, and_7_out, and_8_out, and_9_out, and_10_out);
  or or_5 (MBRtoMAR, and_18_out, and_19_out);
  nor nor_1 (IncTimer, and_13_out, and_14_out, and_15_out, and_16_out, and_17_out);

  assign IncPC = T1;
  assign MBRtoIR = T2;
  assign PCtoMAR = T0;
endmodule
